# Fritzing sketch Gyro Arduino Ckt (saved by Fritzing 0.9.3b)
breadboards: 1

parts:
  Part1 = Arduino Uno (Rev3)
  Part2 = Triple Axis Gyro Breakout ITG-3200

nets:
  N1: Part1.A4/SDA, Part2.SDA
  N2: Part1.A5/SCL, Part2.SCL
  GND: Part1.GND, Part2.GND
  5V: Part1.5V, Part2.VCC, Part2.VLOGIC
